# Fritzing sketch montage 1 led (saved by Fritzing 0.6.4b)

parts:
  Arduino1 = Arduino
  LED1 = LED - 5mm [color="Red (633nm)" package="5 mm [THT]"]
  R1 = Resistor [tolerance=±5% resistance=220 package=THT]

nets:
  GND: Arduino1.GND
  N1: Arduino1.D2, R1.Pin_0
  5V: Arduino1.+5V, LED1.anode
  N2: LED1.cathode, R1.Pin_1
