# Fritzing sketch TP feux de signalisation (saved by Fritzing 0.6.3b)
breadboards: 1

parts:
  Arduino1 = Arduino
  R2 = Resistor [tolerance=±5% resistance=220 package=THT]
  R3 = Resistor [tolerance=±5% resistance=220 package=THT]
  R4 = Resistor [tolerance=±5% resistance=220 package=THT]
  R5 = Resistor [tolerance=±5% resistance=220 package=THT]
  R1 = Resistor [tolerance=±5% resistance=220 package="1206 [SMD]"]
  LED1 = LED - 5mm [color="Red (633nm)" package="5 mm [THT]"]
  LED2 = LED - 5mm [color="Orange (620nm)" package="5 mm [THT]"]
  LED3 = LED - 5mm [color="Green (555nm)" package="5 mm [THT]"]
  LED4 = LED - 5mm [color="Red (633nm)" package="5 mm [THT]"]
  LED5 = LED - 5mm [color="Orange (620nm)" package="5 mm [THT]"]
  R6 = Resistor [tolerance=±5% resistance=220 package=THT]
  LED6 = LED - 5mm [color="Green (555nm)" package="5 mm [THT]"]

nets:
  GND: Arduino1.GND
  N1: Arduino1.D7, R6.Pin_0
  N2: Arduino1.D6, R5.Pin_0
  N3: Arduino1.D5, R4.Pin_0
  N4: Arduino1.D4, R3.Pin_0
  N5: Arduino1.D3, R2.Pin_0
  N6: Arduino1.D2, R1.Pin_0
  5V: Arduino1.+5V, LED1.anode, LED2.anode, LED3.anode, LED4.anode, LED5.anode, LED6.anode
  N7: R2.Pin_1, LED2.cathode
  N8: R3.Pin_1, LED3.cathode
  N9: R4.Pin_1, LED4.cathode
  N10: R5.Pin_1, LED5.cathode
  N11: R1.Pin_1, LED1.cathode
  N12: R6.Pin_1, LED6.cathode
