# Fritzing sketch montage 1 bouton 1 led (saved by Fritzing 0.7.10b)

parts:
  Arduino1 = Arduino
  R1 = Resistor [tolerance=±5% resistance=10k package=THT]
  C1 = Ceramic Capacitor [capacitance=10nF package="100 mil [THT, multilayer]"]
  S1 = Pushbutton [package=THT]
  R2 = Resistor [tolerance=±5% resistance=220 package=THT]
  LED1 = LED - 5mm [color="Red (633nm)" package="5 mm [THT]"]

nets:
  GND: Arduino1.GND, C1.0, S1.leg1
  N1: Arduino1.D13, R2.Pin_0
  N2: Arduino1.D2, R1.Pin_1, C1.1, S1.leg0
  5V: Arduino1.+5V, R1.Pin_0, LED1.anode
  N3: R2.Pin_1, LED1.cathode
