# Fritzing sketch montage 2 boutons 4 leds (saved by Fritzing 0.7.10b)
breadboards: 1

parts:
  Arduino1 = Arduino
  R1 = Resistor [tolerance=±5% resistance=10k package=THT]
  C1 = Ceramic Capacitor [capacitance=10nF package="100 mil [THT, multilayer]"]
  R2 = Resistor [tolerance=±5% resistance=220 package=THT]
  LED1 = LED - 5mm [color="Red (633nm)" package="5 mm [THT]"]
  R3 = Resistor [tolerance=±5% resistance=220 package=THT]
  R4 = Resistor [tolerance=±5% resistance=220 package=THT]
  R5 = Resistor [tolerance=±5% resistance=220 package=THT]
  LED2 = LED - 5mm [color="Red (633nm)" package="5 mm [THT]"]
  LED3 = LED - 5mm [color="Red (633nm)" package="5 mm [THT]"]
  LED4 = LED - 5mm [color="Red (633nm)" package="5 mm [THT]"]
  R6 = Resistor [tolerance=±5% resistance=10k package=THT]
  C2 = Ceramic Capacitor [capacitance=10nF package="100 mil [THT, multilayer]"]
  S1 = Pushbutton [package=THT]
  S2 = Pushbutton [package=THT]

nets:
  GND: Arduino1.GND, C1.0, C2.0, S1.leg1, S2.leg1
  N1: Arduino1.D13, R2.Pin_0
  N2: Arduino1.D12, R3.Pin_0
  N3: Arduino1.D11, R4.Pin_0
  N4: Arduino1.D10, R5.Pin_0
  N5: Arduino1.D3, R6.Pin_1, C2.1, S2.leg0
  N6: Arduino1.D2, R1.Pin_1, C1.1, S1.leg0
  5V: Arduino1.+5V, R1.Pin_0, LED1.anode, LED2.anode, LED3.anode, LED4.anode, R6.Pin_0
  N7: R2.Pin_1, LED1.cathode
  N8: R3.Pin_1, LED2.cathode
  N9: R4.Pin_1, LED3.cathode
  N10: R5.Pin_1, LED4.cathode
