# Fritzing sketch 7 segments et decodeur (saved by Fritzing 0.7.10b)
breadboards: 1

parts:
  DI1 = 7-Segment LED Display [package=THT]
  IC1 = IC, DIP package, 16 pins [chip_label=IC spacing=300mil]
  R1 = Resistor [tolerance=±5% resistance=220 package=THT]
  R2 = Resistor [tolerance=±5% resistance=220 package=THT]
  R3 = Resistor [tolerance=±5% resistance=220 package=THT]
  R4 = Resistor [tolerance=±5% resistance=220 package=THT]
  R5 = Resistor [tolerance=±5% resistance=220 package=THT]
  R6 = Resistor [tolerance=±5% resistance=220 package=THT]
  R7 = Resistor [tolerance=±5% resistance=220 package=THT]
  Arduino1 = Arduino

nets:
  N1: DI1.cathodeE, R7.Pin_1
  N2: DI1.cathodeD, R1.Pin_1
  N3: DI1.commAnode#2, IC1.pin1, IC1.pin6, IC1.pin16, Arduino1.+5V
  N4: DI1.cathodeC, R2.Pin_1
  N5: DI1.cathodeB, R3.Pin_1
  N6: DI1.cathodeA, R6.Pin_0
  N7: DI1.cathodeF, R5.Pin_0
  N8: DI1.cathodeG, R4.Pin_0
  N9: IC1.pin7, IC1.pin8, Arduino1.GND
  N10: IC1.pin9, R7.Pin_0
  N11: IC1.pin10, R1.Pin_0
  N12: IC1.pin11, R2.Pin_0
  N13: IC1.pin12, R3.Pin_0
  N14: IC1.pin13, R6.Pin_1
  N15: IC1.pin14, R5.Pin_1
  N16: IC1.pin15, R4.Pin_1

notes:
  segments [C B D A]
