# Fritzing sketch 7 segments (saved by Fritzing 0.6.3b)
breadboards: 1

parts:
  DI1 = 7-Segment LED Display [package=THT]
  R1 = Resistor [tolerance=±5% resistance=330 package=THT]
  R2 = Resistor [tolerance=±5% resistance=330 package=THT]
  R3 = Resistor [tolerance=±5% resistance=330 package=THT]
  R4 = Resistor [tolerance=±5% resistance=330 package=THT]
  R5 = Resistor [tolerance=±5% resistance=330 package=THT]
  R6 = Resistor [tolerance=±5% resistance=330 package=THT]
  R7 = Resistor [tolerance=±5% resistance=330 package=THT]
  R8 = Resistor [tolerance=±5% resistance=330 package=THT]
  Arduino1 = Arduino  # not connected

nets:
  N1: DI1.cathodeE, R6.Pin_1
  N2: DI1.cathodeD, R2.Pin_1
  N3: DI1.cathodeC, R5.Pin_0
  N4: DI1.cathodeDP, R8.Pin_0
  N5: DI1.cathodeB, R1.Pin_0
  N6: DI1.cathodeA, R4.Pin_0
  N7: DI1.cathodeF, R3.Pin_1
  N8: DI1.cathodeG, R7.Pin_1
