# Fritzing sketch 7 segments (saved by Fritzing 0.7.10b)
breadboards: 1

parts:
  DI1 = 7-Segment LED Display [package=THT]
  R1 = Resistor [tolerance=±5% resistance=330 package=THT]
  R2 = Resistor [tolerance=±5% resistance=330 package=THT]
  R3 = Resistor [tolerance=±5% resistance=330 package=THT]
  R4 = Resistor [tolerance=±5% resistance=330 package=THT]
  R5 = Resistor [tolerance=±5% resistance=330 package=THT]
  R6 = Resistor [tolerance=±5% resistance=330 package=THT]
  R7 = Resistor [tolerance=±5% resistance=330 package=THT]
  Arduino1 = Arduino

nets:
  N1: DI1.cathodeE, R6.Pin_1
  N2: DI1.cathodeD, R2.Pin_1
  N3: DI1.commAnode#2, Arduino1.+5V
  N4: DI1.cathodeC, R5.Pin_0
  N5: DI1.cathodeB, R1.Pin_0
  N6: DI1.cathodeA, R4.Pin_0
  N7: DI1.cathodeF, R3.Pin_1
  N8: DI1.cathodeG, R7.Pin_1
  N9: R1.Pin_1, Arduino1.D3
  N10: R2.Pin_0, Arduino1.D5
  N11: R3.Pin_0, Arduino1.D7
  N12: R4.Pin_1, Arduino1.D2
  N13: R5.Pin_1, Arduino1.D4
  N14: R6.Pin_0, Arduino1.D6
  N15: R7.Pin_0, Arduino1.D8
