# Fritzing sketch TP_Parking (saved by Fritzing 0.6.3b)
breadboards: 2

parts:
  DI1 = 7-Segment LED Display [package=THT]
  DI2 = 7-Segment LED Display [package=THT]
  IC1 = IC, DIP package, 16 pins [chip_label=IC spacing=300mil]
  R1 = Resistor [tolerance=±5% resistance=220 package=THT]
  R2 = Resistor [tolerance=±5% resistance=220 package=THT]
  R3 = Resistor [tolerance=±5% resistance=220 package=THT]
  R4 = Resistor [tolerance=±5% resistance=220 package=THT]
  R5 = Resistor [tolerance=±5% resistance=220 package=THT]
  R6 = Resistor [tolerance=±5% resistance=220 package=THT]
  R7 = Resistor [tolerance=±5% resistance=220 package=THT]
  Arduino1 = Arduino
  Q1 = NPN-Transistor [package="TO92 [THT]"]
  Q2 = NPN-Transistor [package="TO92 [THT]"]
  R8 = Resistor [tolerance=±5% resistance=2.2k package=THT]
  R9 = Resistor [tolerance=±5% resistance=2.2k package=THT]
  LED1 = LED - 5mm [color="Red (633nm)" package="5 mm [THT]"]
  R10 = Resistor [tolerance=±5% resistance=220 package=THT]
  R11 = Resistor [tolerance=±5% resistance=220 package=THT]
  LED2 = LED - 5mm [color="Green (565nm)" package="5 mm [THT]"]
  R12 = Resistor [tolerance=±5% resistance=10k package=THT]
  R13 = Resistor [tolerance=±5% resistance=10k package=THT]
  C2 = Ceramic Capacitor [capacitance=100nF package="100 mil [THT, multilayer]"]
  S1 = Pushbutton [package=THT]
  S2 = Pushbutton [package=THT]
  C3 = Ceramic Capacitor [capacitance=100nF package="100 mil [THT, multilayer]"]

nets:
  N1: DI1.cathodeE, DI2.cathodeE, R1.Pin_1
  N2: DI1.cathodeD, DI2.cathodeD, R2.Pin_1
  N3: DI1.cathodeC, DI2.cathodeC, R4.Pin_1
  N4: DI1.cathodeB, DI2.cathodeB, R3.Pin_1
  N5: DI1.cathodeA, DI2.cathodeA, R5.Pin_0
  N6: DI1.commAnode#7, Q1.C
  N7: DI1.cathodeF, DI2.cathodeF, R7.Pin_0
  N8: DI1.cathodeG, DI2.cathodeG, R6.Pin_0
  N9: DI2.commAnode#2, Q2.C
  N10: IC1.pin1, Arduino1.D3
  N11: IC1.pin2, Arduino1.D4
  N12: IC1.pin3, IC1.pin4, IC1.pin5, IC1.pin16, Arduino1.+5V, Q1.E, Q2.E, R10.Pin_1, R11.Pin_1, R12.Pin_1, R13.Pin_1
  N13: IC1.pin6, Arduino1.D5
  N14: IC1.pin7, Arduino1.D2
  N15: IC1.pin8, Arduino1.GND, C2.0, S1.leg1, S2.leg1, C3.1
  N16: IC1.pin9, R1.Pin_0
  N17: IC1.pin10, R2.Pin_0
  N18: IC1.pin11, R4.Pin_0
  N19: IC1.pin12, R3.Pin_0
  N20: IC1.pin13, R5.Pin_1
  N21: IC1.pin14, R6.Pin_1
  N22: IC1.pin15, R7.Pin_1
  N23: Arduino1.D12, LED1.cathode
  N24: Arduino1.D11, LED2.cathode
  N25: Arduino1.D9, R12.Pin_0, S1.leg0, C3.0
  N26: Arduino1.D8, R13.Pin_0, C2.1, S2.leg0
  N27: Arduino1.D7, R9.Pin_1
  N28: Arduino1.D6, R8.Pin_1
  N29: Q1.B, R8.Pin_0
  N30: Q2.B, R9.Pin_0
  N31: LED1.anode, R11.Pin_0
  N32: R10.Pin_0, LED2.anode
