# Fritzing sketch TP baignade interdite (saved by Fritzing 0.7.10b)
breadboards: 1

parts:
  Arduino1 = Arduino
  R1 = Resistor [tolerance=±5% resistance=220 package=THT]
  R2 = Resistor [tolerance=±5% resistance=220 package=THT]
  R3 = Resistor [tolerance=±5% resistance=220 package=THT]
  LED1 = LED - 5mm [color="Red (633nm)" package="5 mm [THT]"]
  LED2 = LED - 5mm [color="Orange (620nm)" package="5 mm [THT]"]
  LED3 = LED - 5mm [color="Green (565nm)" package="5 mm [THT]"]
  R4 = Resistor [tolerance=±5% resistance=10k package=THT]
  R5 = Resistor [tolerance=±5% resistance=10k package=THT]
  S1 = Pushbutton [package=THT]
  S2 = Pushbutton [package=THT]
  C1 = Ceramic Capacitor [capacitance=10nF package="100 mil [THT, multilayer]"]
  C2 = Ceramic Capacitor [capacitance=10nF package="100 mil [THT, multilayer]"]

nets:
  N1: Arduino1.GND, S1.leg1, S2.leg1, C1.0, C2.0
  N2: Arduino1.D13, R2.Pin_1
  N3: Arduino1.D12, R1.Pin_1
  N4: Arduino1.D11, R3.Pin_1
  N5: Arduino1.D3, R5.Pin_1, S2.leg0, C2.1
  N6: Arduino1.D2, R4.Pin_1, S1.leg0, C1.1
  5V: Arduino1.+5V, LED1.anode, LED2.anode, LED3.anode, R4.Pin_0, R5.Pin_0
  N7: R1.Pin_0, LED2.cathode
  N8: R2.Pin_0, LED1.cathode
  N9: R3.Pin_0, LED3.cathode
