# Fritzing sketch TP vumetre (saved by Fritzing 0.7.10b)
breadboards: 1

parts:
  LED1 = LED - 5mm [color="Red (633nm)" package="5 mm [THT]"]
  LED2 = LED - 5mm [color="Red (633nm)" package="5 mm [THT]"]
  LED3 = LED - 5mm [color="Orange (620nm)" package="5 mm [THT]"]
  LED4 = LED - 5mm [color="Orange (620nm)" package="5 mm [THT]"]
  LED5 = LED - 5mm [color="Green (555nm)" package="5 mm [THT]"]
  LED6 = LED - 5mm [color="Green (555nm)" package="5 mm [THT]"]
  LED7 = LED - 5mm [color="Orange (620nm)" package="5 mm [THT]"]
  LED8 = LED - 5mm [color="Green (555nm)" package="5 mm [THT]"]
  LED9 = LED - 5mm [color="Green (555nm)" package="5 mm [THT]"]
  LED10 = LED - 5mm [color="Green (555nm)" package="5 mm [THT]"]
  R3 = Resistor [tolerance=±5% resistance=220 package=THT]
  R4 = Resistor [tolerance=±5% resistance=220 package=THT]
  R5 = Resistor [tolerance=±5% resistance=220 package=THT]
  R6 = Resistor [tolerance=±5% resistance=220 package=THT]
  R7 = Resistor [tolerance=±5% resistance=220 package=THT]
  R8 = Resistor [tolerance=±5% resistance=220 package=THT]
  R9 = Resistor [tolerance=±5% resistance=220 package=THT]
  R10 = Resistor [tolerance=±5% resistance=220 package=THT]
  R11 = Resistor [tolerance=±5% resistance=220 package=THT]
  R12 = Resistor [tolerance=±5% resistance=220 package=THT]
  Arduino1 = Arduino
  R13 = Rotary Potentiometer (Small) [maximum_resistance=100kΩ]

nets:
  N1: LED1.cathode, R3.Pin_0
  N2: LED1.anode, LED2.anode, LED3.anode, LED4.anode, LED5.anode, LED6.anode, LED7.anode, LED8.anode, LED9.anode, LED10.anode, Arduino1.+5V, R13.leg2
  N3: LED2.cathode, R4.Pin_0
  N4: LED3.cathode, R5.Pin_0
  N5: LED4.cathode, R6.Pin_0
  N6: LED5.cathode, R8.Pin_0
  N7: LED6.cathode, R9.Pin_0
  N8: LED7.cathode, R7.Pin_0
  N9: LED8.cathode, R11.Pin_0
  N10: LED9.cathode, R12.Pin_0
  N11: LED10.cathode, R10.Pin_0
  N12: R3.Pin_1, Arduino1.D11
  N13: R4.Pin_1, Arduino1.D10
  N14: R5.Pin_1, Arduino1.D9
  N15: R6.Pin_1, Arduino1.D8
  N16: R7.Pin_1, Arduino1.D7
  N17: R8.Pin_1, Arduino1.D6
  N18: R9.Pin_1, Arduino1.D5
  N19: R10.Pin_1, Arduino1.D4
  N20: R11.Pin_1, Arduino1.D3
  N21: R12.Pin_1, Arduino1.D2
  N22: Arduino1.GND, R13.leg1
  N23: Arduino1.A0, R13.wiper
