# Fritzing sketch voltmetre (saved by Fritzing 0.7.10b)
breadboards: 1

parts:
  DI1 = 7-Segment LED Display [package=THT]
  DI2 = 7-Segment LED Display [package=THT]
  IC1 = IC, DIP package, 16 pins [chip_label=IC spacing=300mil]
  R1 = Resistor [tolerance=±5% resistance=220 package=THT]
  R2 = Resistor [tolerance=±5% resistance=220 package=THT]
  R3 = Resistor [tolerance=±5% resistance=220 package=THT]
  R4 = Resistor [tolerance=±5% resistance=220 package=THT]
  R5 = Resistor [tolerance=±5% resistance=220 package=THT]
  R6 = Resistor [tolerance=±5% resistance=220 package=THT]
  R7 = Resistor [tolerance=±5% resistance=220 package=THT]
  Arduino1 = Arduino
  Q1 = NPN-Transistor [package="TO92 [THT]"]
  Q2 = NPN-Transistor [package="TO92 [THT]"]
  R8 = Resistor [tolerance=±5% resistance=2.2k package=THT]
  R9 = Resistor [tolerance=±5% resistance=2.2k package=THT]
  R10 = Rotary Potentiometer (Small) [maximum_resistance=100kΩ]

nets:
  N1: DI1.cathodeE, DI2.cathodeE, R1.Pin_1
  N2: DI1.cathodeD, DI2.cathodeD, R2.Pin_1
  N3: DI1.commAnode#2, Q1.C
  N4: DI1.cathodeC, DI2.cathodeC, R4.Pin_1
  N5: DI1.cathodeB, DI2.cathodeB, R3.Pin_1
  N6: DI1.cathodeA, DI2.cathodeA, R5.Pin_0
  N7: DI1.cathodeF, DI2.cathodeF, R7.Pin_0
  N8: DI1.cathodeG, DI2.cathodeG, R6.Pin_0
  N9: DI2.commAnode#2, Q2.C
  N10: IC1.pin1, IC1.pin6, IC1.pin16, Arduino1.+5V, Q1.E, Q2.E, R10.leg2
  N11: IC1.pin2, Arduino1.D4
  N12: IC1.pin3, Arduino1.D3
  N13: IC1.pin4, Arduino1.D5
  N14: IC1.pin5, Arduino1.D2
  N15: IC1.pin7, IC1.pin8, Arduino1.GND, R10.leg1
  N16: IC1.pin9, R1.Pin_0
  N17: IC1.pin10, R2.Pin_0
  N18: IC1.pin11, R4.Pin_0
  N19: IC1.pin12, R3.Pin_0
  N20: IC1.pin13, R5.Pin_1
  N21: IC1.pin14, R6.Pin_1
  N22: IC1.pin15, R7.Pin_1
  N23: Arduino1.D7, R9.Pin_1
  N24: Arduino1.D6, R8.Pin_1
  N25: Arduino1.A0, R10.wiper
  N26: Q1.B, R8.Pin_0
  N27: Q2.B, R9.Pin_0

notes:
  2.2 kO
  220 Ohms
