# Fritzing sketch Led RGB (saved by Fritzing 0.7.10b)
breadboards: 1

parts:
  Arduino1 = Arduino
  LED1 = RGB LED (com. anode, rbg) [package="5 mm [THT]"]
  R1 = Resistor [tolerance=±5% resistance=220 package=THT]
  R2 = Resistor [tolerance=±5% resistance=220 package=THT]
  R3 = Resistor [tolerance=±5% resistance=220 package=THT]

nets:
  N1: Arduino1.D11, R1.Pin_1
  N2: Arduino1.D10, R2.Pin_1
  N3: Arduino1.D9, R3.Pin_1
  N4: Arduino1.+5V, LED1.common_anode
  N5: LED1.red_cathode, R1.Pin_0
  N6: LED1.blue_cathode, R2.Pin_0
  N7: LED1.green_cathode, R3.Pin_0
