# Fritzing sketch 2 LDR et 2 LED (saved by Fritzing 0.8.3b)
breadboards: 1

parts:
  R1 = Resistor [tolerance=±5% resistance=47k package=THT]
  R3 = Photocell (LDR) [package=THT]
  LED1 = LED - 5mm [color="Red (633nm)" package="5 mm [THT]"]
  R4 = Resistor [tolerance=±5% resistance=220 package=THT]
  R5 = Resistor [tolerance=±5% resistance=220 package=THT]
  LED2 = LED - 5mm [color="Red (633nm)" package="5 mm [THT]"]
  R6 = Resistor [tolerance=±5% resistance=47k package=THT]
  R7 = Photocell (LDR) [package=THT]
  Arduino2 = Arduino

nets:
  N1: R1.Pin_0, R3.pin_1, Arduino2.A0
  N2: R1.Pin_1, R4.Pin_1, R5.Pin_1, R6.Pin_1, Arduino2.+5V
  N3: R3.pin_0, R7.pin_0, Arduino2.GND
  N4: LED1.cathode, Arduino2.D2
  N5: LED1.anode, R4.Pin_0
  N6: R5.Pin_0, LED2.anode
  N7: LED2.cathode, Arduino2.D3
  N8: R6.Pin_0, R7.pin_1, Arduino2.A1
