# Fritzing sketch Piezo (saved by Fritzing 0.8.3b)
breadboards: 1

parts:
  Arduino3 = Arduino
  R1 = Resistor [tolerance=±5% resistance=1M package=THT]
  J1 = Piezo Speaker
  R2 = Resistor [tolerance=±5% resistance=220 package=THT]
  LED1 = LED - 5mm [color="Red (633nm)" package="5 mm [THT]"]
  D1 = Zener Diode [part_number=1N4732A breakdown_voltage=4.7V package="300 mil [THT]"]

nets:
  N1: Arduino3.GND, R1.Pin_0, J1.pin1, D1.anode
  N2: Arduino3.D2, LED1.cathode
  N3: Arduino3.+5V, R2.Pin_0
  N4: Arduino3.A0, R1.Pin_1, J1.pin2, D1.cathode
  N5: R2.Pin_1, LED1.anode
