# Fritzing sketch Moteur CC L293 D (saved by Fritzing 0.8.3b)
breadboards: 1

parts:
  Arduino1 = Arduino
  M1 = DC Motor
  VCC1 = Battery block 9V
  L293D = IC, DIP package, 16 pins [chip_label=IC]
  C1 = Electrolytic Capacitor [capacitance=1µF voltage=16V package="100 mil [THT, electrolytic]"]

nets:
  N1: Arduino1.GND, VCC1.-, L293D.pin1, L293D.pin2, L293D.pin4, L293D.pin5, L293D.pin7, L293D.pin12, L293D.pin13, C1.-
  N2: Arduino1.D4, L293D.pin10
  N3: Arduino1.D3, L293D.pin9
  N4: Arduino1.D2, L293D.pin15
  N5: Arduino1.+5V, L293D.pin16
  N6: M1.pin_1, L293D.pin14
  N7: M1.pin_2, L293D.pin11
  N8: VCC1.+, L293D.pin8, C1.+
