# Fritzing sketch Moteur CC L298 (saved by Fritzing 0.8.3b)
breadboards: 1

parts:
  Arduino1 = Arduino
  M1 = DC Motor
  VCC1 = Battery block 9V
  IC1 = L298 Dual Full Bridge Driver
  C2 = Ceramic Capacitor [capacitance=100nF package="100 mil [THT, multilayer]"]
  C3 = Ceramic Capacitor [capacitance=100nF package="100 mil [THT, multilayer]"]
  D1 = Rectifier Diode [part_number=1N4001 package="300 mil [THT]"]
  D3 = Rectifier Diode [part_number=1N4001 package="300 mil [THT]"]
  D4 = Rectifier Diode [part_number=1N4001 package="300 mil [THT]"]
  D2 = Rectifier Diode [part_number=1N4001 breakdown_voltage=3.6V package="300 mil [THT]"]
  C4 = Electrolytic Capacitor [capacitance=1µF package="100 mil [THT, electrolytic]"]

nets:
  N1: Arduino1.GND, VCC1.-, IC1.pin8, IC1.pin10, IC1.pin11, IC1.pin12, C2.0, C3.0, D1.anode, D4.anode, C4.-
  N2: Arduino1.D4, IC1.pin5
  N3: Arduino1.D3, IC1.pin6
  N4: Arduino1.D2, IC1.pin7
  N5: Arduino1.+5V, IC1.pin9, C3.1
  N6: M1.pin_1, IC1.pin2, D3.anode, D4.cathode
  N7: M1.pin_2, IC1.pin3, D1.cathode, D2.anode
  N8: VCC1.+, IC1.pin4, C2.1, D3.cathode, D2.cathode, C4.+

custom parts:
  L298 Dual Full Bridge Driver: L298 Dual Full Bridge Driver in a 15 lead Multiwatt package.
