# Fritzing sketch Moteur CC (saved by Fritzing 0.8.3b)
breadboards: 1

parts:
  Arduino1 = Arduino
  M1 = DC Motor
  R1 = Resistor [tolerance=±5% resistance=10k package=THT]
  VCC1 = Battery block 9V
  C1 = Ceramic Capacitor [capacitance=100nF voltage=16V package="100 mil [THT, multilayer]"]
  D1 = Rectifier Diode [part_number=1N4001 package="300 mil [THT]"]
  Q1 = Basic FET N-Channel [package="TO220 [THT]"]

nets:
  N1: Arduino1.GND, R1.Pin_1, VCC1.-, Q1.source
  N2: Arduino1.D3, R1.Pin_0, Q1.gate
  N3: M1.pin_1, C1.0, D1.anode, Q1.drain
  N4: M1.pin_2, VCC1.+, C1.1, D1.cathode
