# Fritzing sketch Exercice (saved by Fritzing 0.7.10b)

parts:
  Arduino1 = Arduino
  J1 = Basic Servo
  R1 = Rotary Potentiometer (Small) [maximum_resistance=100kΩ]

nets:
  GND: Arduino1.GND, J1.gnd, R1.leg1
  N1: Arduino1.D2, J1.pulse
  +5V: Arduino1.+5V, J1.vcc, R1.leg2
  N2: Arduino1.A0, R1.wiper
