# Fritzing sketch cablage avec L297 (saved by Fritzing 0.8.3b)
breadboards: 2

parts:
  Arduino1 = Arduino
  VCC1 = Battery block 9V
  IC1 = L298 Dual Full Bridge Driver
  C2 = Ceramic Capacitor [capacitance=100nF package="100 mil [THT, multilayer]"]
  C3 = Ceramic Capacitor [capacitance=100nF package="100 mil [THT, multilayer]"]
  C4 = Electrolytic Capacitor [capacitance=1µF package="100 mil [THT, electrolytic]"]
  M1 = Stepper Motor - Bipolar
  D1 = Rectifier Diode [part_number=1N4001 package="300 mil [THT]"]
  D2 = Rectifier Diode [part_number=1N4001 package="300 mil [THT]"]
  D3 = Rectifier Diode [part_number=1N4001 package="300 mil [THT]"]
  D4 = Rectifier Diode [part_number=1N4001 package="300 mil [THT]"]
  D5 = Rectifier Diode [part_number=1N4001 package="300 mil [THT]"]
  D6 = Rectifier Diode [part_number=1N4001 package="300 mil [THT]"]
  D7 = Rectifier Diode [part_number=1N4001 package="300 mil [THT]"]
  D8 = Rectifier Diode [part_number=1N4001 package="300 mil [THT]"]
  IC2 = L297D [part_number="L297-1, L297D"]
  R1 = Resistor [tolerance=±5% resistance=22k package=THT]
  C5 = Ceramic Capacitor [capacitance=33nF package="100 mil [THT, multilayer]"]

nets:
  N1: Arduino1.GND, VCC1.-, IC1.pin8, C2.0, C3.0, C4.-, D1.anode, D2.anode, D3.anode, D4.anode, IC2.Control, IC2.Sens_2, IC2.Sens_1, C5.0
  N2: Arduino1.D4, IC2.H_/F
  N3: Arduino1.D3, IC2./CLK
  N4: Arduino1.D2, IC2.CW_/CCW
  N5: Arduino1.+5V, IC1.pin9, C3.1, IC2.EN, IC2.Vs, IC2.Vref, IC2./RESET, R1.Pin_0
  N6: VCC1.+, IC1.pin4, C2.1, C4.+, D5.cathode, D6.cathode, D7.cathode, D8.cathode
  N7: IC1.pin2, M1.A, D1.cathode, D5.anode
  N8: IC1.pin3, M1.C, D2.cathode, D8.anode
  N9: IC1.pin5, IC2.A
  N10: IC1.pin7, IC2.B
  N11: IC1.pin10, IC2.C
  N12: IC1.pin12, IC2.D
  N13: IC1.pin13, M1.B, D3.cathode, D6.anode
  N14: IC1.pin14, M1.D, D4.cathode, D7.anode
  N15: IC2.OSC, R1.Pin_1, C5.1

custom parts:
  L298 Dual Full Bridge Driver: L298 Dual Full Bridge Driver in a 15 lead Multiwatt package.
  L297D: L297 Steppermotor controller
