# Fritzing sketch cablage bipolaire (saved by Fritzing 0.8.3b)
breadboards: 1

parts:
  Arduino1 = Arduino
  VCC1 = Battery block 9V
  IC1 = L298 Dual Full Bridge Driver
  C2 = Ceramic Capacitor [capacitance=100nF package="100 mil [THT, multilayer]"]
  C3 = Ceramic Capacitor [capacitance=100nF package="100 mil [THT, multilayer]"]
  C4 = Electrolytic Capacitor [capacitance=1µF package="100 mil [THT, electrolytic]"]
  M1 = Stepper Motor - Bipolar
  D1 = Rectifier Diode [part_number=1N4001 package="300 mil [THT]"]
  D2 = Rectifier Diode [part_number=1N4001 package="300 mil [THT]"]
  D3 = Rectifier Diode [part_number=1N4001 package="300 mil [THT]"]
  D4 = Rectifier Diode [part_number=1N4001 package="300 mil [THT]"]
  D5 = Rectifier Diode [part_number=1N4001 package="300 mil [THT]"]
  D6 = Rectifier Diode [part_number=1N4001 package="300 mil [THT]"]
  D7 = Rectifier Diode [part_number=1N4001 package="300 mil [THT]"]
  D8 = Rectifier Diode [part_number=1N4001 package="300 mil [THT]"]

nets:
  N1: Arduino1.GND, VCC1.-, IC1.pin8, C2.0, C3.0, C4.-, D1.anode, D2.anode, D3.anode, D4.anode
  N2: Arduino1.D5, IC1.pin12
  N3: Arduino1.D4, IC1.pin10
  N4: Arduino1.D3, IC1.pin7
  N5: Arduino1.D2, IC1.pin5
  N6: Arduino1.+5V, IC1.pin6, IC1.pin9, IC1.pin11, C3.1
  N7: VCC1.+, IC1.pin4, C2.1, C4.+, D5.cathode, D6.cathode, D7.cathode, D8.cathode
  N8: IC1.pin2, M1.A, D1.cathode, D5.anode
  N9: IC1.pin3, M1.C, D2.cathode, D8.anode
  N10: IC1.pin13, M1.B, D3.cathode, D6.anode
  N11: IC1.pin14, M1.D, D4.cathode, D7.anode

custom parts:
  L298 Dual Full Bridge Driver: L298 Dual Full Bridge Driver in a 15 lead Multiwatt package.
