# Fritzing sketch cablage unipolaire (saved by Fritzing 0.8.3b)
breadboards: 1

parts:
  Arduino1 = Arduino
  VCC1 = Battery block 9V
  M1 = Stepper Motor - Unipolar
  ULN2003A1 = ULN2003A [package="DIP (Dual Inline)"]

nets:
  GND: Arduino1.GND, VCC1.-, ULN2003A1.GND
  N1: Arduino1.D5, ULN2003A1.IN_4
  N2: Arduino1.D4, ULN2003A1.IN_3
  N3: Arduino1.D3, ULN2003A1.IN_2
  N4: Arduino1.D2, ULN2003A1.IN_1
  N5: VCC1.+, M1.COMMON_1, M1.COMMON_2, ULN2003A1.Common_free_wheeling_diodes
  N6: M1.A, ULN2003A1.OUT_1
  N7: M1.C, ULN2003A1.OUT_2
  N8: M1.B, ULN2003A1.OUT_3
  N9: M1.D, ULN2003A1.OUT_4

custom parts:
  ULN2003A: The ULN2001A, ULN2002A, ULN2003 and ULN2004A are high voltage, high current darlington arrays each containing seven open collector darlington pairs with common emitters. Each channel rated at 500mA and can withstand peak currents of 600mA. Suppression diodes are included for inductive load driving and the inputs are pinned opposite the outputs to simplify board layout.
