# Fritzing sketch LCD branchement complet (saved by Fritzing 0.7.10b)

parts:
  Arduino1 = Arduino
  LCD1 = LCD screen
  R1 = Rotary Potentiometer (Small) [maximum_resistance=100kΩ]

nets:
  GND: Arduino1.GND, LCD1.VSS, LCD1.R/W, R1.leg2
  N1: Arduino1.D11, LCD1.RS
  N2: Arduino1.D10, LCD1.E
  N3: Arduino1.D9, LCD1.DB0
  N4: Arduino1.D8, LCD1.DB1
  N5: Arduino1.D7, LCD1.DB2
  N6: Arduino1.D6, LCD1.DB3
  N7: Arduino1.D5, LCD1.DB4
  N8: Arduino1.D4, LCD1.DB5
  N9: Arduino1.D3, LCD1.DB6
  N10: Arduino1.D2, LCD1.DB7
  +5V: Arduino1.+5V, LCD1.VDD, R1.leg1
  N11: LCD1.V0, R1.wiper
