# Fritzing sketch TP Supervision (saved by Fritzing 0.7.10b)
breadboards: 1

parts:
  Arduino1 = Arduino
  LCD1 = LCD screen
  R1 = Rotary Potentiometer (Small) [maximum_resistance=100kΩ]
  R2 = Rotary Potentiometer (Small) [maximum_resistance=100kΩ]
  R3 = Rotary Potentiometer (Small) [maximum_resistance=100kΩ]
  S1 = Pushbutton [package=THT]
  S2 = Pushbutton [package=THT]
  C1 = Ceramic Capacitor [capacitance=10nF package="100 mil [THT, multilayer]"]
  C2 = Ceramic Capacitor [capacitance=10nF package="100 mil [THT, multilayer]"]
  R4 = Resistor [tolerance=±5% resistance=10k package=THT]
  R5 = Resistor [tolerance=±5% resistance=10k package=THT]

nets:
  GND: Arduino1.GND, LCD1.VSS, LCD1.R/W, LCD1.DB0, LCD1.DB1, LCD1.DB2, LCD1.DB3, R1.leg2, R2.leg1, R3.leg1, S1.leg0, S2.leg0, C1.0, C2.0
  N1: Arduino1.D11, LCD1.RS
  N2: Arduino1.D10, LCD1.E
  N3: Arduino1.D8, S2.leg1, C2.1, R5.Pin_1
  N4: Arduino1.D7, S1.leg1, C1.1, R4.Pin_1
  N5: Arduino1.D5, LCD1.DB4
  N6: Arduino1.D4, LCD1.DB5
  N7: Arduino1.D3, LCD1.DB6
  N8: Arduino1.D2, LCD1.DB7
  +5V: Arduino1.+5V, LCD1.VDD, R1.leg1, R2.leg2, R3.leg2, R4.Pin_0, R5.Pin_0
  N9: Arduino1.A0, R2.wiper
  N10: Arduino1.A1, R3.wiper
  N11: LCD1.V0, R1.wiper
